# Fritzing sketch FanCHeck (saved by Fritzing 0.9.3b)
circuit board: 3.2cm x 3.2cm

parts:
  R1 = Resistor [tolerance=±5% resistance=10k package=THT]
  toPC = female pin header, 4 pins [form="♀ (female)"]
  toFAN = male pin header, 4 pins [form="♂ (male)"]
  Q3 = PNP-Transistor [package="TO92 [THT]"]
  Q4 = NPN-Transistor [package="TO92 [THT]"]
  Q5 = NPN-Transistor [package="TO92 [THT]"]
  Q6 = NPN-Transistor [package="TO92 [THT]"]
  Q2 = PNP-Transistor [package="TO92 [THT]"]
  Q1 = PNP-Transistor [package="TO92 [THT]"]
  R2 = Resistor [tolerance=±5% resistance=470 package=THT]
  R3 = Resistor [tolerance=±5% resistance=470 package=THT]
  toBiColorLED = female pin header, 2 pins [form="♀ (female)"]

nets:
  N1: R1.Pin_0, toPC.pin3, toFAN.pin3, Q4.B, Q6.B, Q2.B, Q1.B
  N2: R1.Pin_1, toPC.pin2, toFAN.pin2, Q3.C, Q2.C, Q1.C
  N3: toPC.pin1, toFAN.pin1, Q4.C, Q5.C, Q6.C
  N4: toPC.pin4, toFAN.pin4
  N5: Q3.E, Q5.E, R2.Pin_0
  N6: Q3.B, Q6.E
  N7: Q4.E, Q1.E, R3.Pin_0
  N8: Q5.B, Q2.E
  N9: R2.Pin_1, toBiColorLED.pin1
  N10: R3.Pin_1, toBiColorLED.pin2

notes:
  Yellow-ish:
  LED Colors
  Fan runs Slow
  Red/Green Alt.
  Fan Stopped!
  Red or Green:
  Fan runs fast
